# Fritzing sketch 7th_VOICE (saved by Fritzing 0.9.3b)
circuit board: 5cm x 3.5cm
breadboards: 1

parts:
  IC7 = IC, DIP package, 14 pins [chip_label=LM324]
  J4 = female pin header, 2 pins [form="♀ (female)" part_number="AUDIO IN"]
  J3 = female pin header, 3 pins [form="♀ (female)" part_number=POWER]
  R5 = Resistor [tolerance=±5% resistance=1k package=THT]
  R6 = Resistor [tolerance=±5% resistance=1M package=THT]
  R7 = Resistor [tolerance=±5% resistance=1M package=THT]
  R8 = Resistor [tolerance=±5% resistance=100k package=THT]
  R9 = Resistor [tolerance=±5% resistance=4.7k package=THT]
  J5 = female pin header, 2 pins [form="♀ (female)" part_number=GAIN]
  C7 = Electrolytic Capacitor [capacitance=47µF package="100 mil [THT, electrolytic]"]
  R10 = Resistor [tolerance=±5% resistance=100k package=THT]
  R11 = Resistor [tolerance=±5% resistance=100k package=THT]
  R12 = Resistor [tolerance=±5% resistance=4.7k package=THT]
  D1 = Rectifier Diode [part_number=1N5819 package="300 mil [THT]"]
  D2 = Rectifier Diode [part_number=1N5819 package="300 mil [THT]"]
  R13 = Resistor [tolerance=±5% resistance=4.7k package=THT]
  D3 = Rectifier Diode [part_number=1N5819 package="300 mil [THT]"]
  D4 = Rectifier Diode [part_number=1N5819 package="300 mil [THT]"]
  J7 = female pin header, 2 pins [form="♀ (female)" part_number=7th_VOICE_OUT]
  C10 = Tantalum Capacitor [capacitance=10µF package="100 mil [THT, tantalum]"]
  R14 = Resistor [tolerance=±5% resistance=10k package=THT]
  J6 = female pin header, 3 pins [form="♀ (female)" part_number="ADCs DAC"]
  R2 = Resistor [tolerance=±5% resistance=10k package=THT]
  R3 = Resistor [tolerance=±5% resistance=10k package=THT]
  C4 = Electrolytic Capacitor [capacitance=47µF package="100 mil [THT, electrolytic]"]
  C2 = Electrolytic Capacitor [capacitance=47µF package="100 mil [THT, electrolytic]"]
  C3 = Electrolytic Capacitor [capacitance=47µF package="100 mil [THT, electrolytic]"]
  C11 = Ceramic Capacitor [capacitance=100nF package="200 mil [THT, multilayer]"]
  C9 = Ceramic Capacitor [capacitance=270pF package="200 mil [THT, multilayer]"]
  C8 = Ceramic Capacitor [capacitance=100nF package="200 mil [THT, multilayer]"]
  C6 = Ceramic Capacitor [capacitance=270pF package="200 mil [THT, multilayer]"]
  C5 = Ceramic Capacitor [capacitance=100nF package="200 mil [THT, multilayer]"]

nets:
  OUT_2: IC7.pin1, R8.Pin_1, R12.Pin_0, C8.1, C6.0
  NEG_2: IC7.pin2, R8.Pin_0, R9.Pin_1, C6.1
  POS_2: IC7.pin3, R5.Pin_1
  9V: IC7.pin4, J3.pin2, C2.+
  1.65V/POS_3: IC7.pin5, R6.Pin_1, R2.Pin_1, R3.Pin_1, C4.+
  NEG_3: IC7.pin6, R10.Pin_0, R11.Pin_1, C9.1
  OUT_3: IC7.pin7, R10.Pin_1, R13.Pin_0, C9.0
  NEG_1/OUT_1: IC7.pin8, IC7.pin9, C10.+
  POS_1: IC7.pin10, R14.Pin_1, C11.1
  GND: IC7.pin11, J4.pin1, J3.pin1, R7.Pin_0, C7.-, D1.anode, D3.anode, J7.pin2, R3.Pin_0, C4.-, C2.-, C3.-, C11.0
  POS_4: IC7.pin12
  NEG_4: IC7.pin13
  OUT_4: IC7.pin14
  N1: J4.pin2, R7.Pin_1, C5.1
  3.3V: J3.pin3, D2.cathode, D4.cathode, R2.Pin_0, C3.+
  N2: R5.Pin_0, R6.Pin_0, C5.0
  N3: R9.Pin_0, J5.pin2
  N4: J5.pin1, C7.+
  N5: R11.Pin_0, C8.0
  N6: R12.Pin_1, D1.cathode, D2.anode, J6.pin2
  N7: R13.Pin_1, D3.cathode, D4.anode, J6.pin3
  N8: J7.pin1, C10.-
  N9: R14.Pin_0, J6.pin1

notes:
  CUTOFF
  Poly Sinth, 7th VOICE PCB, 1
