# Fritzing sketch Synth_Shield_PCB (saved by Fritzing 0.9.3b)
breadboards: 1

parts:
  Componente1 = Arduino Due (Rev2b)
  Q1 = 2N7000 FET N-Channel [part_number=2N7000 package=TO92]
  Q2 = 2N7000 FET N-Channel [part_number=2N7000 package=TO92]
  Q3 = 2N7000 FET N-Channel [part_number=2N7000 package=TO92]
  Q4 = 2N7000 FET N-Channel [part_number=2N7000 package=TO92]
  Q5 = 2N7000 FET N-Channel [part_number=2N7000 package=TO92]
  Q6 = 2N7000 FET N-Channel [part_number=2N7000 package=TO92]
  R1 = Resistor [tolerance=±5% resistance=470 package=THT]
  R2 = Resistor [tolerance=±5% resistance=470 package=THT]
  R3 = Resistor [tolerance=±5% resistance=470 package=THT]
  R4 = Resistor [tolerance=±5% resistance=470 package=THT]
  C1 = Ceramic Capacitor [capacitance=100nF package="100 mil [THT, multilayer]"]
  C2 = Ceramic Capacitor [capacitance=100nF package="100 mil [THT, multilayer]"]
  C3 = Ceramic Capacitor [capacitance=100nF package="100 mil [THT, multilayer]"]
  C4 = Ceramic Capacitor [capacitance=100nF package="100 mil [THT, multilayer]"]
  R5 = Resistor [tolerance=±5% resistance=10k package=THT]
  R6 = Resistor [tolerance=±5% resistance=10k package=THT]
  R7 = Resistor [tolerance=±5% resistance=10k package=THT]
  R8 = Resistor [tolerance=±5% resistance=10k package=THT]
  R9 = Resistor [tolerance=±5% resistance=470 package=THT]
  R10 = Resistor [tolerance=±5% resistance=470 package=THT]
  Q7 = NPN-Transistor [package="TO92 [THT]"]
  Q8 = NPN-Transistor [package="TO92 [THT]"]
  Q9 = NPN-Transistor [package="TO92 [THT]"]
  Q10 = NPN-Transistor [package="TO92 [THT]"]
  Q11 = NPN-Transistor [package="TO92 [THT]"]
  Q12 = NPN-Transistor [package="TO92 [THT]"]
  C5 = Ceramic Capacitor [capacitance=100nF package="100 mil [THT, multilayer]"]
  C6 = Ceramic Capacitor [capacitance=100nF package="100 mil [THT, multilayer]"]
  C7 = Ceramic Capacitor [capacitance=100nF package="100 mil [THT, multilayer]"]
  C8 = Ceramic Capacitor [capacitance=100nF package="100 mil [THT, multilayer]"]
  C9 = Ceramic Capacitor [capacitance=100nF package="100 mil [THT, multilayer]"]
  C10 = Ceramic Capacitor [capacitance=100nF package="100 mil [THT, multilayer]"]
  R11 = Resistor [tolerance=±5% resistance=10k package=THT]
  R12 = Resistor [tolerance=±5% resistance=10k package=THT]
  C11 = Ceramic Capacitor [capacitance=100nF package="100 mil [THT, multilayer]"]
  C12 = Ceramic Capacitor [capacitance=100nF package="100 mil [THT, multilayer]"]
  R13 = Resistor [tolerance=±5% resistance=10k package=THT]
  R14 = Resistor [tolerance=±5% resistance=10k package=THT]
  R15 = Resistor [tolerance=±5% resistance=10k package=THT]
  R16 = Resistor [tolerance=±5% resistance=10k package=THT]
  C13 = Ceramic Capacitor [capacitance=100nF package="100 mil [THT, multilayer]"]
  C14 = Ceramic Capacitor [capacitance=100nF package="100 mil [THT, multilayer]"]
  C15 = Ceramic Capacitor [capacitance=100nF package="100 mil [THT, multilayer]"]
  C16 = Ceramic Capacitor [capacitance=100nF package="100 mil [THT, multilayer]"]
  R17 = Resistor [tolerance=±5% resistance=10k package=THT]
  R18 = Resistor [tolerance=±5% resistance=10k package=THT]
  C17 = Ceramic Capacitor [capacitance=100nF package="100 mil [THT, multilayer]"]
  C18 = Ceramic Capacitor [capacitance=100nF package="100 mil [THT, multilayer]"]
  IC1 = Voltage Regulator [package=78xxl]
  C19 = Ceramic Capacitor [capacitance=100nF package="100 mil [THT, multilayer]"]
  C20 = Electrolytic Capacitor [capacitance=47µF voltage=16V package="100 mil [THT, electrolytic]"]
  C21 = Ceramic Capacitor [capacitance=100nF package="100 mil [THT, multilayer]"]
  C22 = Electrolytic Capacitor [capacitance=100µF voltage=16V package="100 mil [THT, electrolytic]"]
  J2 = female pin header, 2 pins [form="♀ (female)" part_number="VIN 12V"]
  U2 = Optocoupler [part_number=4N28 package=THT]
  J3 = female pin header, 2 pins [form="♀ (female)"]
  D6 = Diode [part_number=1N4148 package=diode-1n4148]
  R19 = Resistor [tolerance=±5% resistance=330 package=THT]
  C23 = Tantalum Capacitor [capacitance=3.3µF package="200 mil [THT, tantalum]"]
  Q13 = NPN-Transistor [part_number=BC548 package="TO92 [THT]"]
  Q14 = NPN-Transistor [part_number=BC548 package="TO92 [THT]"]
  D7 = Diode [part_number=1N4148 package=diode-1n4148]
  D8 = Diode [part_number=1N4148 package=diode-1n4148]
  D9 = Diode [part_number=1N4148 package=diode-1n4148]
  D10 = Diode [part_number=1N4148 package=diode-1n4148]
  R20 = Resistor [tolerance=±5% resistance=220 package=THT]
  R21 = Resistor [tolerance=±5% resistance=330 package=THT]
  R22 = Resistor [tolerance=±5% resistance=330 package=THT]
  R23 = Resistor [tolerance=±5% resistance=1k package=THT]
  C24 = Ceramic Capacitor [capacitance=2.2nF package="200 mil [THT, multilayer]"]
  C25 = Ceramic Capacitor [capacitance=2.2nF package="200 mil [THT, multilayer]"]
  C26 = Ceramic Capacitor [capacitance=2.2nF package="200 mil [THT, multilayer]"]
  R24 = Resistor [tolerance=±5% resistance=1k package=THT]
  R25 = Resistor [tolerance=±5% resistance=1k package=THT]
  C27 = Ceramic Capacitor [capacitance=100nF package="100 mil [THT, multilayer]"]
  R26 = Resistor [tolerance=±5% resistance=1k package=THT]
  R27 = Resistor [tolerance=±5% resistance=1M package=THT]
  R28 = Rotary Potentiometer (Large) [maximum_resistance=10kΩ package=THT]
  R29 = Resistor [tolerance=±5% resistance=27k package=THT]
  R30 = Resistor [tolerance=±5% resistance=22k package=THT]
  R31 = Resistor [tolerance=±5% resistance=220 package=THT]
  Q15 = NPN-Transistor [part_number=BC548 package="TO92 [THT]"]
  Q16 = NPN-Transistor [package="TO92 [THT]"]
  R32 = Resistor [tolerance=±5% resistance=10k package=THT]
  R33 = Resistor [tolerance=±5% resistance=220 package=THT]
  R34 = Resistor [tolerance=±5% resistance=220 package=THT]
  J4 = female pin header, 2 pins [form="♀ (female)"]
  R35 = Resistor [tolerance=±5% resistance=10k package=THT]
  IC3 = IC, DIP package, 14 pins [chip_label=IC]  # not connected
  R36 = Resistor [tolerance=±5% resistance=470 package=THT]
  R37 = Resistor [tolerance=±5% resistance=470 package=THT]
  C28 = Electrolytic Capacitor [capacitance=47µF voltage=16V package="100 mil [THT, electrolytic]"]
  IC4 = IC, DIP package, 8 pins [chip_label=24LC256 part_number=24LC256]
  R38 = Resistor [tolerance=±5% resistance=10k package=THT]
  R39 = Resistor [tolerance=±5% resistance=10k package=THT]

nets:
  N1: Componente1.D16/TX2, R35.Pin_0
  N2: Componente1.D17/RX2, U2.Pin_5, R31.Pin_0
  3.3V: Componente1.IOREF, R31.Pin_1, IC4.pin8, R38.Pin_1, R39.Pin_1
  5V: Componente1.5V, Q7.C, Q8.C, Q9.C, Q10.C, Q11.C, Q12.C, R32.Pin_1, R34.Pin_0
  GND: Componente1.GND, Q1.source, Q2.source, Q3.source, Q4.source, Q5.source, Q6.source, C1.0, C2.0, C3.0, C4.0, C5.0, C6.0, C7.0, C8.1, C9.1, C10.1, C11.0, C12.0, C13.0, C14.0, C15.0, C16.0, C17.0, C18.0, IC1.GND, C19.0, C20.-, C21.0, C22.-, J2.pin2, U2.Pin_4, R23.Pin_1, R25.Pin_1, R28.leg1, Q15.E, Q16.E, R37.Pin_0, C28.-, IC4.pin1, IC4.pin2, IC4.pin3, IC4.pin4, IC4.pin7
  9V: Componente1.VIN, IC1.OUT, C19.1, C20.+, R20.Pin_0, R28.leg2, R36.Pin_0
  N3: Componente1.D10_PWM/SS0, R12.Pin_1
  N4: Componente1.D11_PWM, R11.Pin_1
  I2C_SCL: Componente1.SDA1, IC4.pin6, R38.Pin_0
  I2C_SDA: Componente1.SCL1, IC4.pin5, R39.Pin_0
  N5: Componente1.D2_PWM, R5.Pin_0
  N6: Componente1.D3_PWM, R6.Pin_0
  N7: Componente1.D4_PWM/SS1, R7.Pin_0
  N8: Componente1.D5_PWM, R8.Pin_0
  N9: Componente1.D6_PWM, Q3.gate
  N10: Componente1.D7_PWM, Q4.gate
  N11: Componente1.D34, Q2.gate
  N12: Componente1.D36, Q1.gate
  N13: Componente1.D38, Q5.gate
  N14: Componente1.D40, Q6.gate
  N15: Q1.drain, R1.Pin_0, R16.Pin_0
  N16: Q2.drain, R2.Pin_0, R15.Pin_0
  N17: Q3.drain, R3.Pin_0, R14.Pin_0
  N18: Q4.drain, R4.Pin_0, R13.Pin_0
  N19: Q5.drain, R9.Pin_0, R18.Pin_1
  N20: Q6.drain, R10.Pin_0, R17.Pin_1
  N21: R1.Pin_1, C1.1, Q7.E
  N22: R2.Pin_1, C2.1, Q8.E
  N23: R3.Pin_1, C3.1, Q9.E
  N24: R4.Pin_1, C4.1, Q10.E
  N25: R5.Pin_1, Q7.B, C7.1
  N26: R6.Pin_1, Q8.B, C8.0
  N27: R7.Pin_1, Q9.B, C9.0
  N28: R8.Pin_1, Q10.B, C10.0
  N29: R9.Pin_1, Q12.E, C6.1
  N30: R10.Pin_1, Q11.E, C5.1
  N31: Q11.B, R12.Pin_0, C12.1
  N32: Q12.B, R11.Pin_0, C11.1
  N33: R13.Pin_1, C16.1
  N34: R14.Pin_1, C15.1
  N35: R15.Pin_1, C14.1
  N36: R16.Pin_1, C13.1
  N37: R17.Pin_0, C18.1
  N38: R18.Pin_0, C17.1
  N39: IC1.IN, C21.1
  N40: C22.+, J2.pin1
  N41: U2.Pin_1, D6.C, R19.Pin_0
  N42: U2.Pin_2, J3.pin2, D6.A
  N43: J3.pin1, R19.Pin_1
  N44: C23.-, C25.0, R25.Pin_0
  VCO_OUT: C23.+
  N45: Q13.E, Q14.E, R23.Pin_0
  N46: Q13.B, R26.Pin_1, R29.Pin_1, R30.Pin_1
  N47: Q13.C, D10.C, R22.Pin_1
  4.5V: Q14.B, R26.Pin_0, R27.Pin_1, R36.Pin_1, R37.Pin_1, C28.+
  N48: Q14.C, D7.A, R21.Pin_1
  N49: D7.C, D8.A, C24.1
  N50: D8.C, D9.A, C25.1, C27.0
  N51: D9.C, D10.A, C26.1
  N52: R20.Pin_1, R21.Pin_0, R22.Pin_0
  N53: C24.0, C26.0, R24.Pin_0
  FILTER_OUT: C27.1, R27.Pin_0
  N54: R28.wiper, R29.Pin_0
  LFO_EG2_OUT: R30.Pin_0
  N55: Q15.B, R35.Pin_1
  N56: Q15.C, Q16.B, R32.Pin_0
  N57: Q16.C, R33.Pin_0
  N58: R33.Pin_1, J4.pin2
  N59: R34.Pin_1, J4.pin1

notes:
  MIDI IN
  CUTOFF
  MIDI OUT

custom parts:
  2N7000 FET N-Channel: A 2N7000 MOSFET N-Channel Transistor
