# Fritzing sketch VCF (saved by Fritzing 0.9.3b)
circuit board: 5cm x 10cm
breadboards: 1

parts:
  Q13 = NPN-Transistor [part_number=BC548 package="TO92 [THT]"]
  Q14 = NPN-Transistor [part_number=BC548 package="TO92 [THT]"]
  D7 = Diode [part_number=1N4148 package=diode-1n4148]
  D8 = Diode [part_number=1N4148 package=diode-1n4148]
  D9 = Diode [part_number=1N4148 package=diode-1n4148]
  D10 = Diode [part_number=1N4148 package=diode-1n4148]
  R20 = Resistor [tolerance=±5% resistance=220 package=THT]
  R21 = Resistor [tolerance=±5% resistance=330 package=THT]
  R22 = Resistor [tolerance=±5% resistance=330 package=THT]
  R23 = Resistor [tolerance=±5% resistance=470 package=THT]
  C24 = Ceramic Capacitor [capacitance=2.2nF package="200 mil [THT, multilayer]"]
  C25 = Ceramic Capacitor [capacitance=4.7nF package="200 mil [THT, multilayer]"]
  C26 = Ceramic Capacitor [capacitance=2.2nF package="200 mil [THT, multilayer]"]
  R24 = Resistor [tolerance=±5% resistance=1k package=THT]
  R25 = Resistor [tolerance=±5% resistance=1k package=THT]
  R26 = Resistor [tolerance=±5% resistance=1k package=THT]
  R27 = Resistor [tolerance=±5% resistance=330k package=THT]
  R29 = Resistor [tolerance=±5% resistance=10k package=THT]
  R30 = Resistor [tolerance=±5% resistance=33k package=THT]
  R52 = Resistor [tolerance=±5% resistance=82k package=THT]
  R55 = Resistor [tolerance=±5% resistance=4.7k package=THT]
  R56 = Resistor [tolerance=±5% resistance=22k package=THT]
  25KB = female pin header, 3 pins [form="♀ (female)"]
  CUTOFF = female pin header, 3 pins [form="♀ (female)" part_number=10KA]
  10KA = female pin header, 3 pins [form="♀ (female)" part_number="ADSR DEEP"]
  R57 = Resistor [tolerance=±5% resistance=5.6k package=THT]
  C44 = Electrolytic Capacitor [capacitance=2.2µF package="100 mil [THT, electrolytic]"]
  AU_OUT = female pin header, 2 pins [form="♀ (female)"]
  R58 = Resistor [tolerance=±5% resistance=5.6k package=THT]
  10KA_2 = female pin header, 3 pins [form="♀ (female)"]
  R59 = Resistor [tolerance=±5% resistance=33k package=THT]
  R62 = Resistor [tolerance=±5% resistance=10k package=THT]
  R63 = Resistor [tolerance=±5% resistance=100k package=THT]
  R64 = Resistor [tolerance=±5% resistance=47k package=THT]
  C46 = Electrolytic Capacitor [capacitance=47µF package="100 mil [THT, electrolytic]"]
  D11 = Rectifier Diode [part_number=1N4148 package="300 mil [THT]"]
  D12 = Rectifier Diode [part_number=1N4148 package="300 mil [THT]"]
  SIGNALS = female pin header, 3 pins [form="♀ (female)"]
  POWER = female pin header, 2 pins [form="♀ (female)" part_number="9V IN"]
  C47 = Electrolytic Capacitor [capacitance=100µF package="100 mil [THT, electrolytic]"]
  R65 = Resistor [tolerance=±5% resistance=470 package=THT]
  R66 = Resistor [tolerance=±5% resistance=470 package=THT]
  C49 = Electrolytic Capacitor [capacitance=47µF package="100 mil [THT, electrolytic]"]
  AU_IN = female pin header, 2 pins [form="♀ (female)"]
  C51 = Electrolytic Capacitor [capacitance=47µF package="100 mil [THT, electrolytic]"]
  R67 = Resistor [tolerance=±5% resistance=3.3k package=THT]
  IC6 = IC, DIP package, 14 pins [chip_label=LM324]
  C43 = Ceramic Capacitor [capacitance=100nF package="200 mil [THT, multilayer]"]
  C45 = Ceramic Capacitor [capacitance=100nF package="200 mil [THT, multilayer]"]
  C48 = Ceramic Capacitor [capacitance=100nF package="200 mil [THT, multilayer]"]
  C50 = Ceramic Capacitor [capacitance=100nF package="200 mil [THT, multilayer]"]
  C27 = Ceramic Capacitor [capacitance=100nF package="200 mil [THT, multilayer]"]
  C42 = Ceramic Capacitor [capacitance=100pF package="200 mil [THT, multilayer]"]
  R68 = Resistor [tolerance=±5% resistance=100 package=THT]
  R69 = Resistor [tolerance=±5% resistance=100 package=THT]

nets:
  N1: Q13.E, Q14.E, R23.Pin_0
  N2: Q13.B, R26.Pin_1, R29.Pin_1, R30.Pin_1, R59.Pin_1
  N3: Q13.C, D10.C, R22.Pin_1
  4.5V/POS_1: Q14.B, R26.Pin_0, R27.Pin_1, R65.Pin_1, R66.Pin_1, C49.+, IC6.pin10, C50.1
  N4: Q14.C, D7.A, R21.Pin_1
  N5: D7.C, D8.A, C24.1
  N6: D8.C, D9.A, C25.1, C27.0
  N7: D9.C, D10.A, C26.1
  9V: R20.Pin_0, CUTOFF.pin3, POWER.pin2, C47.+, R65.Pin_0, IC6.pin4, C48.1
  N8: R20.Pin_1, R21.Pin_0, R22.Pin_0, C51.+
  GND: R23.Pin_1, R25.Pin_1, 10KA.pin1, AU_OUT.pin2, 10KA_2.pin1, R63.Pin_0, R64.Pin_0, C46.-, SIGNALS.pin1, POWER.pin1, C47.-, R66.Pin_0, C49.-, AU_IN.pin1, IC6.pin11, C43.0, C45.0, C48.0, C50.0
  N9: C24.0, C26.0, R24.Pin_0
  N10: C25.0, R25.Pin_0
  OUT_3: R24.Pin_1, 25KB.pin1, R62.Pin_0, IC6.pin7, R68.Pin_1, R69.Pin_1
  POS_3: R27.Pin_0, IC6.pin5, C27.1
  N11: R29.Pin_0, CUTOFF.pin2
  N12: R30.Pin_0, 10KA.pin2
  NEG_1: R52.Pin_0, R62.Pin_1, IC6.pin9, C42.1
  OUT_1: R52.Pin_1, C44.+, IC6.pin8, C42.0
  NEG_3: R55.Pin_0, R56.Pin_1, D11.cathode, D12.anode, IC6.pin6
  N13: R55.Pin_1, 25KB.pin2, 25KB.pin3
  N14: R56.Pin_0, C46.+
  N15: CUTOFF.pin1, R64.Pin_1
  NEG_2/OUT_2: 10KA.pin3, IC6.pin1, IC6.pin2
  ADSR_FILTER: R57.Pin_0, SIGNALS.pin3
  POS_2: R57.Pin_1, IC6.pin3, C43.1
  N16: C44.-, AU_OUT.pin1, R63.Pin_1
  LFO_OUT: R58.Pin_0, SIGNALS.pin2
  POS_4: R58.Pin_1, IC6.pin12, C45.1
  N17: 10KA_2.pin2, R59.Pin_0
  NEG_4/OUT_4: 10KA_2.pin3, IC6.pin13, IC6.pin14
  N18: D11.anode, R69.Pin_0
  N19: D12.cathode, R68.Pin_0
  N20: AU_IN.pin2, R67.Pin_0
  N21: C51.-, R67.Pin_1

notes:
  CUTOFF
  LM324_1
  RESONANCE
  LFO DEEP
