# Fritzing sketch VOICES (saved by Fritzing 0.9.3b)
circuit board: 10cm x 8cm
breadboards: 1

parts:
  R1 = Resistor [tolerance=±5% resistance=470 package=THT]
  R2 = Resistor [tolerance=±5% resistance=470 package=THT]
  R3 = Resistor [tolerance=±5% resistance=470 package=THT]
  R4 = Resistor [tolerance=±5% resistance=470 package=THT]
  R5 = Resistor [tolerance=±5% resistance=10k package=THT]
  R6 = Resistor [tolerance=±5% resistance=10k package=THT]
  R7 = Resistor [tolerance=±5% resistance=10k package=THT]
  R8 = Resistor [tolerance=±5% resistance=10k package=THT]
  Q7 = NPN-Transistor [part_number=BC548 package="TO92 [THT]"]
  Q8 = NPN-Transistor [part_number=BC548 package="TO92 [THT]"]
  Q9 = NPN-Transistor [part_number=BC548 package="TO92 [THT]"]
  Q10 = NPN-Transistor [part_number=BC548 package="TO92 [THT]"]
  R13 = Resistor [tolerance=±5% resistance=10k package=THT]
  R14 = Resistor [tolerance=±5% resistance=10k package=THT]
  R15 = Resistor [tolerance=±5% resistance=10k package=THT]
  R16 = Resistor [tolerance=±5% resistance=10k package=THT]
  Q18 = NPN-Transistor [part_number=BC548 package="TO92 [THT]"]
  R40 = Resistor [tolerance=±5% resistance=470 package=THT]
  R41 = Resistor [tolerance=±5% resistance=470 package=THT]
  Q20 = NPN-Transistor [part_number=BC548 package="TO92 [THT]"]
  R42 = Resistor [tolerance=±5% resistance=10k package=THT]
  R43 = Resistor [tolerance=±5% resistance=10k package=THT]
  R44 = Resistor [tolerance=±5% resistance=10k package=THT]
  R45 = Resistor [tolerance=±5% resistance=10k package=THT]
  R46 = Resistor [tolerance=±5% resistance=100k package=THT]
  R47 = Resistor [tolerance=±5% resistance=100k package=THT]
  R48 = Resistor [tolerance=±5% resistance=100k package=THT]
  R49 = Resistor [tolerance=±5% resistance=100k package=THT]
  R50 = Resistor [tolerance=±5% resistance=100k package=THT]
  R51 = Resistor [tolerance=±5% resistance=100k package=THT]
  R52 = Resistor [tolerance=±5% resistance=33k package=THT]
  C44 = Electrolytic Capacitor [capacitance=2.2µF package="100 mil [THT, electrolytic]"]
  10KA = female pin header, 3 pins [form="♀ (female)"]
  J5 = female pin header, 2 pins [form="♀ (female)" part_number="AUDIO OUT"]
  C46 = Electrolytic Capacitor [capacitance=2.2µF package="100 mil [THT, electrolytic]"]
  R60 = Resistor [tolerance=±5% resistance=10k package=THT]
  R61 = Resistor [tolerance=±5% resistance=100k package=THT]
  R62 = Resistor [tolerance=±5% resistance=100k package=THT]
  C50 = Electrolytic Capacitor [capacitance=2.2µF package="100 mil [THT, electrolytic]"]
  R63 = Resistor [tolerance=±5% resistance=100k package=THT]
  R69 = Resistor [tolerance=±5% resistance=100k package=THT]
  R70 = Resistor [tolerance=±5% resistance=100k package=THT]
  J6 = female pin header, 2 pins [form="♀ (female)" part_number="AUX IN 1"]
  R71 = Resistor [tolerance=±5% resistance=100k package=THT]
  J7 = female pin header, 2 pins [form="♀ (female)" part_number="AUDIO OUT PRE FADER"]
  SAMPLES_AUDIO_IN = female pin header, 2 pins [form="♀ (female)"]
  J8 = female pin header, 2 pins [form="♀ (female)" part_number="AUX IN 2"]
  J9 = female pin header, 2 pins [form="♀ (female)" part_number="VOICES OUT"]
  C7 = Ceramic Capacitor [capacitance=100nF package="200 mil [THT, multilayer]"]
  C8 = Ceramic Capacitor [capacitance=100nF package="200 mil [THT, multilayer]"]
  C9 = Ceramic Capacitor [capacitance=100nF package="200 mil [THT, multilayer]"]
  C10 = Ceramic Capacitor [capacitance=100nF package="200 mil [THT, multilayer]"]
  C32 = Ceramic Capacitor [capacitance=100nF package="200 mil [THT, multilayer]"]
  C31 = Ceramic Capacitor [capacitance=100nF package="200 mil [THT, multilayer]"]
  C2 = Ceramic Capacitor [capacitance=100nF package="200 mil [THT, multilayer]"]
  C3 = Ceramic Capacitor [capacitance=100nF package="200 mil [THT, multilayer]"]
  C4 = Ceramic Capacitor [capacitance=100nF package="200 mil [THT, multilayer]"]
  C29 = Ceramic Capacitor [capacitance=100nF package="200 mil [THT, multilayer]"]
  C30 = Ceramic Capacitor [capacitance=100nF package="200 mil [THT, multilayer]"]
  C13 = Ceramic Capacitor [capacitance=100nF package="200 mil [THT, multilayer]"]
  C15 = Ceramic Capacitor [capacitance=100nF package="200 mil [THT, multilayer]"]
  C14 = Ceramic Capacitor [capacitance=100nF package="200 mil [THT, multilayer]"]
  C33 = Ceramic Capacitor [capacitance=100nF package="200 mil [THT, multilayer]"]
  C34 = Ceramic Capacitor [capacitance=100nF package="200 mil [THT, multilayer]"]
  C16 = Ceramic Capacitor [capacitance=100nF package="200 mil [THT, multilayer]"]
  Q23 = MOSFET-NCHANNEL [package=to-92]
  Q24 = MOSFET-NCHANNEL [package=to-92]
  Q25 = MOSFET-NCHANNEL [package=to-92]
  Q26 = MOSFET-NCHANNEL [package=to-92]
  Q27 = MOSFET-NCHANNEL [package=to-92]
  Q28 = MOSFET-NCHANNEL [package=to-92]
  C41 = Ceramic Capacitor [capacitance=100nF package="200 mil [THT, multilayer]"]
  C40 = Ceramic Capacitor [capacitance=100nF package="200 mil [THT, multilayer]"]
  C39 = Ceramic Capacitor [capacitance=100nF package="200 mil [THT, multilayer]"]
  C36 = Ceramic Capacitor [capacitance=100nF package="200 mil [THT, multilayer]"]
  C38 = Ceramic Capacitor [capacitance=100nF package="200 mil [THT, multilayer]"]
  C37 = Ceramic Capacitor [capacitance=100nF package="200 mil [THT, multilayer]"]
  ADSRs = female pin header, 7 pins [form="♀ (female)"]
  VOICEs = female pin header, 7 pins [form="♀ (female)"]
  R72 = Resistor [tolerance=±5% resistance=560 package=THT]
  R73 = Resistor [tolerance=±5% resistance=470 package=THT]
  C57 = Electrolytic Capacitor [capacitance=47µF package="100 mil [THT, electrolytic]"]
  C59 = Electrolytic Capacitor [capacitance=47µF package="100 mil [THT, electrolytic]"]
  POWER = female pin header, 3 pins [form="♀ (female)"]
  C60 = Electrolytic Capacitor [capacitance=47µF package="100 mil [THT, electrolytic]"]
  C58 = Ceramic Capacitor [capacitance=100nF package="200 mil [THT, multilayer]"]
  C48 = Ceramic Capacitor [capacitance=100nF package="200 mil [THT, multilayer]"]
  C42 = Ceramic Capacitor [capacitance=220pF package="200 mil [THT, multilayer]"]
  C55 = Ceramic Capacitor [capacitance=100nF package="200 mil [THT, multilayer]"]
  IC6 = IC, DIP package, 14 pins [chip_label=IC part_number=LM324]
  C47 = Ceramic Capacitor [capacitance=82pF package="200 mil [THT, multilayer]"]
  C56 = Ceramic Capacitor [capacitance=100nF package="200 mil [THT, multilayer]"]
  C61 = Ceramic Capacitor [capacitance=100nF package="200 mil [THT, multilayer]"]

nets:
  N1: R1.Pin_0, R16.Pin_0, Q28.D
  N2: R1.Pin_1, Q7.E, C58.1
  N3: R2.Pin_0, R15.Pin_0, Q27.D
  N4: R2.Pin_1, Q8.E, C2.1
  N5: R3.Pin_0, R14.Pin_0, Q26.D
  N6: R3.Pin_1, Q9.E, C3.1
  N7: R4.Pin_0, R13.Pin_0, Q25.D
  N8: R4.Pin_1, Q10.E, C4.1
  N9: R5.Pin_0, ADSRs.pin2
  N10: R5.Pin_1, Q7.B, C7.1
  N11: R6.Pin_0, ADSRs.pin3
  N12: R6.Pin_1, Q8.B, C8.0
  N13: R7.Pin_0, ADSRs.pin4
  N14: R7.Pin_1, Q9.B, C9.0
  N15: R8.Pin_0, ADSRs.pin5
  N16: R8.Pin_1, Q10.B, C10.0
  5V: Q7.C, Q8.C, Q9.C, Q10.C, Q18.C, Q20.C, POWER.pin2, C60.+, C61.1
  N17: R13.Pin_1, C16.1, C38.1
  N18: R14.Pin_1, C15.1, C39.1
  N19: R15.Pin_1, C14.1, C40.1
  N20: R16.Pin_1, C13.1, C41.1
  N21: Q18.E, R40.Pin_1, C29.1
  N22: Q18.B, R42.Pin_1, C31.0
  N23: R40.Pin_0, R44.Pin_0, Q24.D
  N24: R41.Pin_0, R45.Pin_0, Q23.D
  N25: R41.Pin_1, Q20.E, C30.1
  N26: Q20.B, R43.Pin_1, C32.0
  N27: R42.Pin_0, ADSRs.pin6
  N28: R43.Pin_0, ADSRs.pin7
  N29: R44.Pin_1, C33.1, C37.1
  N30: R45.Pin_1, C34.1, C36.1
  N31: R46.Pin_0, C36.0
  NEG_1: R46.Pin_1, R47.Pin_1, R48.Pin_1, R49.Pin_1, R50.Pin_1, R51.Pin_1, R52.Pin_0, R62.Pin_1, C42.1, IC6.pin2
  N32: R47.Pin_0, C37.0
  N33: R48.Pin_0, C38.0
  N34: R49.Pin_0, C39.0
  N35: R50.Pin_0, C40.0
  N36: R51.Pin_0, C41.0
  OUT_1: R52.Pin_1, J9.pin1, C42.0, IC6.pin1
  N37: C44.-, J5.pin1, R63.Pin_1
  OUT_3: C44.+, R70.Pin_1, IC6.pin8
  GND: 10KA.pin1, J5.pin2, R63.Pin_0, J6.pin1, J7.pin1, SAMPLES_AUDIO_IN.pin1, J8.pin1, J9.pin2, C7.0, C8.1, C9.1, C10.1, C32.1, C31.1, C2.0, C3.0, C4.0, C29.0, C30.0, C13.0, C15.0, C14.0, C33.0, C34.0, C16.0, Q23.S, Q24.S, Q25.S, Q26.S, Q27.S, Q28.S, ADSRs.pin1, VOICEs.pin1, R73.Pin_0, C57.-, C59.-, POWER.pin1, C60.-, C58.0, IC6.pin11, IC6.pin12, C61.0
  N38: 10KA.pin2, C55.1
  N39: 10KA.pin3, C50.-
  N40: C46.-, R60.Pin_0
  N41: C46.+, J8.pin2
  NEG_2: R60.Pin_1, R61.Pin_0, R71.Pin_1, IC6.pin6, C47.1
  OUT_2: R61.Pin_1, C50.+, J7.pin2, IC6.pin7, C47.0
  N42: R62.Pin_0, C48.1
  N43: R69.Pin_0, C55.0
  NEG_3: R69.Pin_1, R70.Pin_0, IC6.pin9
  N44: J6.pin2, C56.0
  N45: R71.Pin_0, C56.1
  N46: SAMPLES_AUDIO_IN.pin2, C48.0
  N47: Q23.G, VOICEs.pin7
  N48: Q24.G, VOICEs.pin6
  N49: Q25.G, VOICEs.pin5
  N50: Q26.G, VOICEs.pin4
  N51: Q27.G, VOICEs.pin3
  N52: Q28.G, VOICEs.pin2
  9V: R72.Pin_0, C59.+, POWER.pin3, IC6.pin4
  4.5V/POS_1/POS_2/POS_3: R72.Pin_1, R73.Pin_1, C57.+, IC6.pin3, IC6.pin5, IC6.pin10
  OUT_4: IC6.pin13, IC6.pin14

notes:
  CUTOFF
  LM324_1
  MASTER VOL

custom parts:
  MOSFET-NCHANNEL: Generic NMOS footprint
