# Fritzing sketch MAIN (saved by Fritzing 0.9.3b)
circuit board: 20cm x 10cm
breadboards: 1

parts:
  R1 = Resistor [tolerance=±5% resistance=470 package=THT]
  R2 = Resistor [tolerance=±5% resistance=470 package=THT]
  R3 = Resistor [tolerance=±5% resistance=470 package=THT]
  R4 = Resistor [tolerance=±5% resistance=470 package=THT]
  R5 = Resistor [tolerance=±5% resistance=10k package=THT]
  R6 = Resistor [tolerance=±5% resistance=10k package=THT]
  R7 = Resistor [tolerance=±5% resistance=10k package=THT]
  R8 = Resistor [tolerance=±5% resistance=10k package=THT]
  Q7 = NPN-Transistor [part_number=BC548 package="TO92 [THT]"]
  Q8 = NPN-Transistor [part_number=BC548 package="TO92 [THT]"]
  Q9 = NPN-Transistor [part_number=BC548 package="TO92 [THT]"]
  Q10 = NPN-Transistor [part_number=BC548 package="TO92 [THT]"]
  R13 = Resistor [tolerance=±5% resistance=10k package=THT]
  R14 = Resistor [tolerance=±5% resistance=10k package=THT]
  R15 = Resistor [tolerance=±5% resistance=10k package=THT]
  R16 = Resistor [tolerance=±5% resistance=10k package=THT]
  C20 = Electrolytic Capacitor [capacitance=100µF voltage=16V package="100 mil [THT, electrolytic]"]
  C22 = Electrolytic Capacitor [capacitance=100µF voltage=16V package="100 mil [THT, electrolytic]"]
  J2 = female pin header, 2 pins [form="♀ (female)" part_number="VIN 12V"]
  U2 = Optocoupler [part_number=4N28 package=THT]
  J3 = female pin header, 2 pins [form="♀ (female)"]
  D6 = Diode [part_number=1N4148 package=diode-1n4148]
  R19 = Resistor [tolerance=±5% resistance=330 package=THT]
  R31 = Resistor [tolerance=±5% resistance=2.2k package=THT]
  Q15 = NPN-Transistor [part_number=BC548 package="TO92 [THT]"]
  Q16 = NPN-Transistor [part_number=BC548 package="TO92 [THT]"]
  R32 = Resistor [tolerance=±5% resistance=10k package=THT]
  R33 = Resistor [tolerance=±5% resistance=220 package=THT]
  R34 = Resistor [tolerance=±5% resistance=220 package=THT]
  J4 = female pin header, 2 pins [form="♀ (female)"]
  R35 = Resistor [tolerance=±5% resistance=10k package=THT]
  R36 = Resistor [tolerance=±5% resistance=560 package=THT]
  R37 = Resistor [tolerance=±5% resistance=470 package=THT]
  C28 = Electrolytic Capacitor [capacitance=100µF voltage=16V package="100 mil [THT, electrolytic]"]
  IC4 = IC, DIP package, 8 pins [chip_label=24LC256 part_number=24LC256]
  Q18 = NPN-Transistor [part_number=BC548 package="TO92 [THT]"]
  R40 = Resistor [tolerance=±5% resistance=470 package=THT]
  R41 = Resistor [tolerance=±5% resistance=470 package=THT]
  Q20 = NPN-Transistor [part_number=BC548 package="TO92 [THT]"]
  R42 = Resistor [tolerance=±5% resistance=10k package=THT]
  R43 = Resistor [tolerance=±5% resistance=10k package=THT]
  R44 = Resistor [tolerance=±5% resistance=10k package=THT]
  R45 = Resistor [tolerance=±5% resistance=10k package=THT]
  ENCODER_A = female pin header, 3 pins [form="♀ (female)"]
  C35 = Electrolytic Capacitor [capacitance=10µF package="100 mil [THT, electrolytic]"]
  ENCODER_B = female pin header, 3 pins [form="♀ (female)"]
  ENCODER_C = female pin header, 3 pins [form="♀ (female)"]
  ENCODER_D = female pin header, 3 pins [form="♀ (female)"]
  LCD_CONN = female pin header, 3 pins [form="♀ (female)"]
  IC5 = LM324 [package=dil16]
  R46 = Resistor [tolerance=±5% resistance=100k package=THT]
  R47 = Resistor [tolerance=±5% resistance=100k package=THT]
  R48 = Resistor [tolerance=±5% resistance=100k package=THT]
  R49 = Resistor [tolerance=±5% resistance=100k package=THT]
  R50 = Resistor [tolerance=±5% resistance=100k package=THT]
  R51 = Resistor [tolerance=±5% resistance=100k package=THT]
  R52 = Resistor [tolerance=±5% resistance=33k package=THT]
  C42 = Ceramic Capacitor [capacitance=220pF package="100 mil [THT, multilayer]"]
  C44 = Electrolytic Capacitor [capacitance=2.2µF package="100 mil [THT, electrolytic]"]
  10KA = female pin header, 3 pins [form="♀ (female)"]
  J5 = female pin header, 2 pins [form="♀ (female)" part_number="AUDIO OUT"]
  C46 = Electrolytic Capacitor [capacitance=2.2µF package="100 mil [THT, electrolytic]"]
  R60 = Resistor [tolerance=±5% resistance=10k package=THT]
  R61 = Resistor [tolerance=±5% resistance=100k package=THT]
  C47 = Ceramic Capacitor [capacitance=82pF package="100 mil [THT, multilayer]"]
  R62 = Resistor [tolerance=±5% resistance=100k package=THT]
  C48 = Ceramic Capacitor [capacitance=100nF package="100 mil [THT, multilayer]"]
  C50 = Electrolytic Capacitor [capacitance=2.2µF package="100 mil [THT, electrolytic]"]
  R63 = Resistor [tolerance=±5% resistance=100k package=THT]
  R69 = Resistor [tolerance=±5% resistance=100k package=THT]
  R70 = Resistor [tolerance=±5% resistance=100k package=THT]
  C55 = Ceramic Capacitor [capacitance=100nF package="100 mil [THT, multilayer]"]
  J6 = female pin header, 2 pins [form="♀ (female)" part_number="AUX IN 1"]
  R71 = Resistor [tolerance=±5% resistance=100k package=THT]
  ANALOG_INS = female pin header, 9 pins [form="♀ (female)"]
  AUDIO_DIFF_IN = female pin header, 3 pins [form="♀ (female)"]
  POWER_OUT = female pin header, 4 pins [form="♀ (female)"]
  J7 = female pin header, 2 pins [form="♀ (female)" part_number="AUDIO OUT PRE FADER"]
  R72 = Resistor [tolerance=±5% resistance=220 package=THT]
  R73 = Resistor [tolerance=±5% resistance=10k package=THT]
  R74 = Resistor [tolerance=±5% resistance=220 package=THT]
  EXPRESSION_PEDAL_INPUT = female pin header, 3 pins [form="♀ (female)"]
  R75 = Resistor [tolerance=±5% resistance=220 package=THT]
  SUSTAIN_PEDAL_INPUT = female pin header, 2 pins [form="♀ (female)"]
  R76 = Resistor [tolerance=±5% resistance=10k package=THT]
  Q21 = NPN-Transistor [part_number=BC548 package="TO92 [THT]"]
  R77 = Resistor [tolerance=±5% resistance=10k package=THT]
  SYNC_IN = female pin header, 2 pins [form="♀ (female)"]
  R78 = Resistor [tolerance=±5% resistance=100k package=THT]
  Q22 = NPN-Transistor [part_number=BC548 package="TO92 [THT]"]
  R79 = Resistor [tolerance=±5% resistance=10k package=THT]
  R80 = Resistor [tolerance=±5% resistance=1k package=THT]
  SYNC_OUT = female pin header, 2 pins [form="♀ (female)"]
  R81 = Resistor [tolerance=±5% resistance=1M package=THT]
  OLED = female pin header, 7 pins [form="♀ (female)"]
  ARDUINO_SPI = female pin header, 3 pins [form="♀ (female)"]
  SDCARD = female pin header, 6 pins [form="♀ (female)"]
  R82 = Resistor [tolerance=±5% resistance=1k package=THT]
  R83 = Resistor [tolerance=±5% resistance=1k package=THT]
  SAMPLES_AUDIO_OUT = female pin header, 3 pins [form="♀ (female)"]
  SAMPLES_AUDIO_IN = female pin header, 2 pins [form="♀ (female)"]
  TO_FILTER = female pin header, 3 pins [form="♀ (female)"]
  J8 = female pin header, 2 pins [form="♀ (female)" part_number="AUX IN 2"]
  C56 = Ceramic Capacitor [capacitance=100nF package="100 mil [THT, multilayer]"]
  J9 = female pin header, 2 pins [form="♀ (female)" part_number="VOICES OUT"]
  Componente1 = Arduino Due (Rev2b)
  FREE_PWMs = female pin header, 3 pins [form="♀ (female)"]
  FREE_UARTs = female pin header, 7 pins [form="♀ (female)"]
  FREE_GPIOs = female pin header, 5 pins [form="♀ (female)"]
  IC1 = Voltage Regulator [package=to220-igo]
  C21 = Ceramic Capacitor [capacitance=100nF package="200 mil [THT, multilayer]"]
  C19 = Ceramic Capacitor [capacitance=100nF package="200 mil [THT, multilayer]"]
  C7 = Ceramic Capacitor [capacitance=100nF package="200 mil [THT, multilayer]"]
  C8 = Ceramic Capacitor [capacitance=100nF package="200 mil [THT, multilayer]"]
  C9 = Ceramic Capacitor [capacitance=100nF package="200 mil [THT, multilayer]"]
  C10 = Ceramic Capacitor [capacitance=100nF package="200 mil [THT, multilayer]"]
  C32 = Ceramic Capacitor [capacitance=100nF package="200 mil [THT, multilayer]"]
  C31 = Ceramic Capacitor [capacitance=100nF package="200 mil [THT, multilayer]"]
  C1 = Ceramic Capacitor [capacitance=100nF package="200 mil [THT, multilayer]"]
  C2 = Ceramic Capacitor [capacitance=100nF package="200 mil [THT, multilayer]"]
  C3 = Ceramic Capacitor [capacitance=100nF package="200 mil [THT, multilayer]"]
  C4 = Ceramic Capacitor [capacitance=100nF package="200 mil [THT, multilayer]"]
  C29 = Ceramic Capacitor [capacitance=100nF package="200 mil [THT, multilayer]"]
  C30 = Ceramic Capacitor [capacitance=100nF package="200 mil [THT, multilayer]"]
  C13 = Ceramic Capacitor [capacitance=100nF package="200 mil [THT, multilayer]"]
  C15 = Ceramic Capacitor [capacitance=100nF package="200 mil [THT, multilayer]"]
  C14 = Ceramic Capacitor [capacitance=100nF package="200 mil [THT, multilayer]"]
  C33 = Ceramic Capacitor [capacitance=100nF package="200 mil [THT, multilayer]"]
  C34 = Ceramic Capacitor [capacitance=100nF package="200 mil [THT, multilayer]"]
  C16 = Ceramic Capacitor [capacitance=100nF package="200 mil [THT, multilayer]"]
  Q23 = MOSFET-NCHANNEL [package=to-92]
  Q24 = MOSFET-NCHANNEL [package=to-92]
  Q25 = MOSFET-NCHANNEL [package=to-92]
  Q26 = MOSFET-NCHANNEL [package=to-92]
  Q27 = MOSFET-NCHANNEL [package=to-92]
  Q28 = MOSFET-NCHANNEL [package=to-92]
  C41 = Ceramic Capacitor [capacitance=100nF package="200 mil [THT, multilayer]"]
  C40 = Ceramic Capacitor [capacitance=100nF package="200 mil [THT, multilayer]"]
  C39 = Ceramic Capacitor [capacitance=100nF package="200 mil [THT, multilayer]"]
  C36 = Ceramic Capacitor [capacitance=100nF package="200 mil [THT, multilayer]"]
  C38 = Ceramic Capacitor [capacitance=100nF package="200 mil [THT, multilayer]"]
  C37 = Ceramic Capacitor [capacitance=100nF package="200 mil [THT, multilayer]"]

nets (from the schematic view):
  N1: R1.Pin_0, R16.Pin_0, Q28.D
  N2: R1.Pin_1, Q7.E, C1.1
  N3: R2.Pin_0, R15.Pin_0, Q27.D
  N4: R2.Pin_1, Q8.E, C2.1
  N5: R3.Pin_0, R14.Pin_0, Q26.D
  N6: R3.Pin_1, Q9.E, C3.1
  N7: R4.Pin_0, R13.Pin_0, Q25.D
  N8: R4.Pin_1, Q10.E, C4.1
  VCA_3: R5.Pin_0, Componente1.D2_PWM
  N9: R5.Pin_1, Q7.B, C7.1
  VCA_2: R6.Pin_0, Componente1.D3_PWM
  N10: R6.Pin_1, Q8.B, C8.0
  VCA_1: R7.Pin_0, Componente1.D4_PWM/SS1
  N11: R7.Pin_1, Q9.B, C9.0
  VCA_0: R8.Pin_0, Componente1.D5_PWM
  N12: R8.Pin_1, Q10.B, C10.0
  5V: Q7.C, Q8.C, Q9.C, Q10.C, R32.Pin_1, R34.Pin_0, Q18.C, Q20.C, POWER_OUT.pin4, R80.Pin_1, SDCARD.pin2, Componente1.5V
  N13: R13.Pin_1, C16.1, C38.1
  N14: R14.Pin_1, C15.1, C39.1
  N15: R15.Pin_1, C14.1, C40.1
  N16: R16.Pin_1, C13.1, C41.1
  GND: C20.-, C22.-, J2.pin2, U2.Pin_4, Q15.E, Q16.E, R37.Pin_0, C28.-, IC4.pin1, IC4.pin2, IC4.pin3, IC4.pin4, IC4.pin7, ENCODER_A.pin2, C35.-, ENCODER_B.pin2, ENCODER_C.pin2, ENCODER_D.pin2, IC5.GND, 10KA.pin1, J5.pin2, R63.Pin_0, J6.pin1, AUDIO_DIFF_IN.pin2, POWER_OUT.pin1, J7.pin1, EXPRESSION_PEDAL_INPUT.pin3, SUSTAIN_PEDAL_INPUT.pin2, Q21.E, SYNC_IN.pin2, R78.Pin_1, Q22.E, SYNC_OUT.pin2, R81.Pin_0, OLED.pin1, SDCARD.pin1, R83.Pin_0, SAMPLES_AUDIO_OUT.pin3, SAMPLES_AUDIO_IN.pin1, TO_FILTER.pin3, J8.pin1, J9.pin2, Componente1.GND, FREE_PWMs.pin3, FREE_UARTs.pin7, FREE_GPIOs.pin5, IC1.GND, C21.0, C19.0, C7.0, C8.1, C9.1, C10.1, C32.1, C31.1, C1.0, C2.0, C3.0, C4.0, C29.0, C30.0, C13.0, C15.0, C14.0, C33.0, C34.0, C16.0, Q27.S, Q28.S
  9V: C20.+, R36.Pin_0, IC5.V+, POWER_OUT.pin2, Componente1.VIN, IC1.OUT, C19.1
  N17: C22.+, J2.pin1
  N18: U2.Pin_1, D6.C, R19.Pin_0
  N19: U2.Pin_2, J3.pin2, D6.A
  RX_MIDI: U2.Pin_5, R31.Pin_0, Componente1.D17/RX2
  N20: J3.pin1, R19.Pin_1
  3.3V: R31.Pin_1, IC4.pin8, POWER_OUT.pin3, R73.Pin_1, R75.Pin_1, R76.Pin_1, OLED.pin2, Componente1.IOREF
  N21: Q15.B, R35.Pin_1
  N22: Q15.C, Q16.B, R32.Pin_0
  N23: Q16.C, R33.Pin_0
  N24: R33.Pin_1, J4.pin2
  N25: R34.Pin_1, J4.pin1
  TX_MIDI: R35.Pin_0, Componente1.D16/TX2
  4.5V/POS_1/POS_2/POS_3: R36.Pin_1, R37.Pin_1, C28.+, IC5.IN1+, IC5.IN2+, IC5.IN3+
  I2C_SDA: IC4.pin5, Componente1.D20/SDA3
  I2C_SCL: IC4.pin6, Componente1.D21/SCL3
  N26: Q18.E, R40.Pin_1, C29.1
  N27: Q18.B, R42.Pin_1, C31.0
  N28: R40.Pin_0, R44.Pin_0, Q24.D
  N29: R41.Pin_0, R45.Pin_0, Q23.D
  N30: R41.Pin_1, Q20.E, C30.1
  N31: Q20.B, R43.Pin_1, C32.0
  VCA_5: R42.Pin_0, Componente1.D10_PWM/SS0
  VCA_4: R43.Pin_0, Componente1.D11_PWM
  N32: R44.Pin_1, C33.1, C37.1
  N33: R45.Pin_1, C34.1, C36.1
  ENCODER_A_1: ENCODER_A.pin1, Componente1.D33
  ENCODER_A_2: ENCODER_A.pin3, Componente1.D35
  N34: C35.+, Componente1.MASTER-RESET
  ENCODER_B_1: ENCODER_B.pin1, Componente1.D37
  ENCODER_B_2: ENCODER_B.pin3, Componente1.D39
  ENCODER_C_1: ENCODER_C.pin1, Componente1.D41
  ENCODER_C_2: ENCODER_C.pin3, Componente1.D43
  ENCODER_D_1: ENCODER_D.pin1, Componente1.D45
  ENCODER_D_2: ENCODER_D.pin3, Componente1.D47
  LCD_RES: LCD_CONN.pin1, OLED.pin5, Componente1.D49
  LCD_CS: LCD_CONN.pin2, OLED.pin7, Componente1.D53
  LCD_DC: LCD_CONN.pin3, OLED.pin6, Componente1.D51
  OUT_1: IC5.OUT1, R52.Pin_1, C42.0, J9.pin1
  NEG_1: IC5.IN1-, R46.Pin_1, R47.Pin_1, R48.Pin_1, R49.Pin_1, R50.Pin_1, R51.Pin_1, R52.Pin_0, C42.1, R62.Pin_1
  NEG_2: IC5.IN2-, R60.Pin_1, R61.Pin_0, C47.1, R71.Pin_1
  OUT_2: IC5.OUT2, R61.Pin_1, C47.0, C50.+, J7.pin2
  OUT_3: IC5.OUT3, C44.+, R70.Pin_1
  NEG_3: IC5.IN3-, R69.Pin_1, R70.Pin_0
  POS_4: IC5.IN4+
  NEG_4: IC5.IN4-
  OUT_4: IC5.OUT4
  N35: R46.Pin_0, C36.0
  N36: R47.Pin_0, C37.0
  N37: R48.Pin_0, C38.0
  N38: R49.Pin_0, C39.0
  N39: R50.Pin_0, C40.0
  N40: R51.Pin_0, C41.0
  N41: C44.-, J5.pin1, R63.Pin_1
  N42: 10KA.pin2, C55.1
  N43: 10KA.pin3, C50.-
  N44: C46.-, R60.Pin_0
  N45: C46.+, J8.pin2
  N46: R62.Pin_0, C48.1
  N47: C48.0, SAMPLES_AUDIO_IN.pin2
  N48: R69.Pin_0, C55.0
  N49: J6.pin2, C56.0
  N50: R71.Pin_0, C56.1
  N51: ANALOG_INS.pin1, Componente1.A11
  N52: ANALOG_INS.pin2, Componente1.A10
  N53: ANALOG_INS.pin3, Componente1.A9
  N54: ANALOG_INS.pin4, Componente1.A8
  N55: ANALOG_INS.pin5, Componente1.A7
  N56: ANALOG_INS.pin6, Componente1.A6
  N57: ANALOG_INS.pin7, Componente1.A5
  N58: ANALOG_INS.pin8, Componente1.A4
  N59: ANALOG_INS.pin9, Componente1.A3
  AUDIO_IN_2: AUDIO_DIFF_IN.pin1, Componente1.A1
  AUDIO_IN_1: AUDIO_DIFF_IN.pin3, Componente1.A0
  PEDAL_SUS: R72.Pin_0, Componente1.D46
  N60: R72.Pin_1, R73.Pin_0, SUSTAIN_PEDAL_INPUT.pin1
  PEDAL_EXP: R74.Pin_0, Componente1.A2
  N61: R74.Pin_1, EXPRESSION_PEDAL_INPUT.pin2, R81.Pin_1
  N62: EXPRESSION_PEDAL_INPUT.pin1, R75.Pin_0
  SYNC_IN: R76.Pin_0, Q21.C, Componente1.D48
  N63: Q21.B, R77.Pin_0, R78.Pin_0
  N64: R77.Pin_1, SYNC_IN.pin1
  N65: Q22.B, R79.Pin_1
  N66: Q22.C, R80.Pin_0, SYNC_OUT.pin1
  SYNC_OUT: R79.Pin_0, Componente1.D50
  CLK: OLED.pin3, ARDUINO_SPI.pin2, SDCARD.pin5
  MOSI: OLED.pin4, ARDUINO_SPI.pin1, SDCARD.pin4
  MISO: ARDUINO_SPI.pin3, R82.Pin_0, R83.Pin_1
  N67: SDCARD.pin3, R82.Pin_1
  SD_CS: SDCARD.pin6
  AUDIO_OUT_1: SAMPLES_AUDIO_OUT.pin1, Componente1.DAC0
  AUDIO_OUT_2: SAMPLES_AUDIO_OUT.pin2, Componente1.DAC1
  ADSR_FILTER: TO_FILTER.pin1, Componente1.D12_PWM
  LFO_OUT: TO_FILTER.pin2, Componente1.D13_PWM
  N68: Componente1.D14/TX3, FREE_UARTs.pin3
  N69: Componente1.D15/RX3, FREE_UARTs.pin4
  N70: Componente1.D18/TX1, FREE_UARTs.pin5
  N71: Componente1.D19/RX1, FREE_UARTs.pin6
  N72: Componente1.D8_PWM, FREE_PWMs.pin2
  N73: Componente1.D9_PWM, FREE_PWMs.pin1
  N74: Componente1.D0/RX, FREE_UARTs.pin1
  N75: Componente1.D1/TX, FREE_UARTs.pin2
  VOICE_4: Componente1.D6_PWM, Q24.G
  VOICE_5: Componente1.D7_PWM, Q23.G
  N76: Componente1.D23, FREE_GPIOs.pin1
  N77: Componente1.D25, FREE_GPIOs.pin2
  N78: Componente1.D27, FREE_GPIOs.pin3
  N79: Componente1.D29, FREE_GPIOs.pin4
  VOICE_0: Componente1.D34, Q28.G
  VOICE_1: Componente1.D36, Q27.G
  VOICE_2: Componente1.D38, Q26.G
  VOICE_3: Componente1.D40, Q25.G
  N80: IC1.IN, C21.1
  N81: Q23.S, Q24.S, Q25.S, Q26.S

notes:
  MIDI IN
  CUTOFF
  MIDI OUT
  LM324_1
  MASTER VOL

custom parts:
  LM324: LM324 Quad OpAmp
  MOSFET-NCHANNEL: Generic NMOS footprint
