# Fritzing sketch Synth_Shield_PCB (saved by Fritzing 0.9.3b)
breadboards: 1

parts:
  Componente1 = Arduino Due (Rev2b)
  Q1 = 2N7000 FET N-Channel [part_number=2N7000 package=TO92]
  Q2 = 2N7000 FET N-Channel [part_number=2N7000 package=TO92]
  Q3 = 2N7000 FET N-Channel [part_number=2N7000 package=TO92]
  Q4 = 2N7000 FET N-Channel [part_number=2N7000 package=TO92]
  R1 = Resistor [tolerance=±5% resistance=470 package=THT]
  R2 = Resistor [tolerance=±5% resistance=470 package=THT]
  R3 = Resistor [tolerance=±5% resistance=470 package=THT]
  R4 = Resistor [tolerance=±5% resistance=470 package=THT]
  C1 = Ceramic Capacitor [capacitance=100nF package="100 mil [THT, multilayer]"]
  C2 = Ceramic Capacitor [capacitance=100nF package="100 mil [THT, multilayer]"]
  C3 = Ceramic Capacitor [capacitance=100nF package="100 mil [THT, multilayer]"]
  C4 = Ceramic Capacitor [capacitance=100nF package="100 mil [THT, multilayer]"]
  R5 = Resistor [tolerance=±5% resistance=10k package=THT]
  R6 = Resistor [tolerance=±5% resistance=10k package=THT]
  R7 = Resistor [tolerance=±5% resistance=10k package=THT]
  R8 = Resistor [tolerance=±5% resistance=10k package=THT]
  Q7 = NPN-Transistor [part_number=BC548 package="TO92 [THT]"]
  Q8 = NPN-Transistor [part_number=BC548 package="TO92 [THT]"]
  Q9 = NPN-Transistor [part_number=BC548 package="TO92 [THT]"]
  Q10 = NPN-Transistor [part_number=BC548 package="TO92 [THT]"]
  C7 = Ceramic Capacitor [capacitance=100nF package="100 mil [THT, multilayer]"]
  C8 = Ceramic Capacitor [capacitance=100nF package="100 mil [THT, multilayer]"]
  C9 = Ceramic Capacitor [capacitance=100nF package="100 mil [THT, multilayer]"]
  C10 = Ceramic Capacitor [capacitance=100nF package="100 mil [THT, multilayer]"]
  R13 = Resistor [tolerance=±5% resistance=10k package=THT]
  R14 = Resistor [tolerance=±5% resistance=10k package=THT]
  R15 = Resistor [tolerance=±5% resistance=10k package=THT]
  R16 = Resistor [tolerance=±5% resistance=10k package=THT]
  C13 = Ceramic Capacitor [capacitance=100nF package="100 mil [THT, multilayer]"]
  C14 = Ceramic Capacitor [capacitance=100nF package="100 mil [THT, multilayer]"]
  C15 = Ceramic Capacitor [capacitance=100nF package="100 mil [THT, multilayer]"]
  C16 = Ceramic Capacitor [capacitance=100nF package="100 mil [THT, multilayer]"]
  IC1 = Voltage Regulator [package=78xxl]
  C19 = Ceramic Capacitor [capacitance=100nF package="100 mil [THT, multilayer]"]
  C20 = Electrolytic Capacitor [capacitance=100µF voltage=16V package="100 mil [THT, electrolytic]"]
  C21 = Ceramic Capacitor [capacitance=100nF package="100 mil [THT, multilayer]"]
  C22 = Electrolytic Capacitor [capacitance=100µF voltage=16V package="100 mil [THT, electrolytic]"]
  J2 = female pin header, 2 pins [form="♀ (female)" part_number="VIN 12V"]
  U2 = Optocoupler [part_number=4N28 package=THT]
  J3 = female pin header, 2 pins [form="♀ (female)"]
  D6 = Diode [part_number=1N4148 package=diode-1n4148]
  R19 = Resistor [tolerance=±5% resistance=330 package=THT]
  Q13 = NPN-Transistor [part_number=BC548 package="TO92 [THT]"]
  Q14 = NPN-Transistor [part_number=BC548 package="TO92 [THT]"]
  D7 = Diode [part_number=1N4148 package=diode-1n4148]
  D8 = Diode [part_number=1N4148 package=diode-1n4148]
  D9 = Diode [part_number=1N4148 package=diode-1n4148]
  D10 = Diode [part_number=1N4148 package=diode-1n4148]
  R20 = Resistor [tolerance=±5% resistance=220 package=THT]
  R21 = Resistor [tolerance=±5% resistance=330 package=THT]
  R22 = Resistor [tolerance=±5% resistance=330 package=THT]
  R23 = Resistor [tolerance=±5% resistance=1k package=THT]
  C24 = Ceramic Capacitor [capacitance=2.2nF package="200 mil [THT, multilayer]"]
  C25 = Ceramic Capacitor [capacitance=2.2nF package="200 mil [THT, multilayer]"]
  C26 = Ceramic Capacitor [capacitance=2.2nF package="200 mil [THT, multilayer]"]
  R24 = Resistor [tolerance=±5% resistance=1k package=THT]
  R25 = Resistor [tolerance=±5% resistance=1k package=THT]
  C27 = Ceramic Capacitor [capacitance=100nF package="100 mil [THT, multilayer]"]
  R26 = Resistor [tolerance=±5% resistance=1k package=THT]
  R27 = Resistor [tolerance=±5% resistance=1M package=THT]
  R29 = Resistor [tolerance=±5% resistance=22k package=THT]
  R30 = Resistor [tolerance=±5% resistance=22k package=THT]
  R31 = Resistor [tolerance=±5% resistance=2.2k package=THT]
  Q15 = NPN-Transistor [part_number=BC548 package="TO92 [THT]"]
  Q16 = NPN-Transistor [part_number=BC548 package="TO92 [THT]"]
  R32 = Resistor [tolerance=±5% resistance=10k package=THT]
  R33 = Resistor [tolerance=±5% resistance=220 package=THT]
  R34 = Resistor [tolerance=±5% resistance=220 package=THT]
  J4 = female pin header, 2 pins [form="♀ (female)"]
  R35 = Resistor [tolerance=±5% resistance=10k package=THT]
  R36 = Resistor [tolerance=±5% resistance=560 package=THT]
  R37 = Resistor [tolerance=±5% resistance=470 package=THT]
  C28 = Electrolytic Capacitor [capacitance=100µF voltage=16V package="100 mil [THT, electrolytic]"]
  IC4 = IC, DIP package, 8 pins [chip_label=24LC256 part_number=24LC256]
  Q17 = 2N7000 FET N-Channel [part_number=2N7000 package=TO92]
  Q18 = NPN-Transistor [part_number=BC548 package="TO92 [THT]"]
  R40 = Resistor [tolerance=±5% resistance=470 package=THT]
  C29 = Ceramic Capacitor [capacitance=100nF package="100 mil [THT, multilayer]"]
  Q19 = 2N7000 FET N-Channel [part_number=2N7000 package=TO92]
  R41 = Resistor [tolerance=±5% resistance=470 package=THT]
  Q20 = NPN-Transistor [part_number=BC548 package="TO92 [THT]"]
  C30 = Ceramic Capacitor [capacitance=100nF package="100 mil [THT, multilayer]"]
  R42 = Resistor [tolerance=±5% resistance=10k package=THT]
  R43 = Resistor [tolerance=±5% resistance=10k package=THT]
  C31 = Ceramic Capacitor [capacitance=100nF package="100 mil [THT, multilayer]"]
  C32 = Ceramic Capacitor [capacitance=100nF package="100 mil [THT, multilayer]"]
  R44 = Resistor [tolerance=±5% resistance=10k package=THT]
  R45 = Resistor [tolerance=±5% resistance=10k package=THT]
  C33 = Ceramic Capacitor [capacitance=100nF package="100 mil [THT, multilayer]"]
  C34 = Ceramic Capacitor [capacitance=100nF package="100 mil [THT, multilayer]"]
  ENCODER_A = female pin header, 3 pins [form="♀ (female)"]
  C35 = Electrolytic Capacitor [capacitance=10µF package="100 mil [THT, electrolytic]"]
  ENCODER_B = female pin header, 3 pins [form="♀ (female)"]
  ENCODER_C = female pin header, 3 pins [form="♀ (female)"]
  ENCODER_D = female pin header, 3 pins [form="♀ (female)"]
  LCD_CONN = female pin header, 3 pins [form="♀ (female)"]
  IC5 = LM324 [package=dil16]
  C36 = Ceramic Capacitor [capacitance=100nF package="100 mil [THT, multilayer]"]
  R46 = Resistor [tolerance=±5% resistance=100k package=THT]
  C37 = Ceramic Capacitor [capacitance=100nF package="100 mil [THT, multilayer]"]
  R47 = Resistor [tolerance=±5% resistance=100k package=THT]
  C38 = Ceramic Capacitor [capacitance=100nF package="100 mil [THT, multilayer]"]
  R48 = Resistor [tolerance=±5% resistance=100k package=THT]
  C39 = Ceramic Capacitor [capacitance=100nF package="100 mil [THT, multilayer]"]
  R49 = Resistor [tolerance=±5% resistance=100k package=THT]
  R50 = Resistor [tolerance=±5% resistance=100k package=THT]
  C40 = Ceramic Capacitor [capacitance=100nF package="100 mil [THT, multilayer]"]
  C41 = Ceramic Capacitor [capacitance=100nF package="100 mil [THT, multilayer]"]
  R51 = Resistor [tolerance=±5% resistance=100k package=THT]
  R52 = Resistor [tolerance=±5% resistance=33k package=THT]
  C42 = Ceramic Capacitor [capacitance=220pF package="100 mil [THT, multilayer]"]
  R53 = Resistor [tolerance=±5% resistance=15k package=THT]
  R55 = Resistor [tolerance=±5% resistance=10k package=THT]
  R56 = Resistor [tolerance=±5% resistance=22k package=THT]
  10KA = female pin header, 3 pins [form="♀ (female)"]
  10KA_2 = female pin header, 3 pins [form="♀ (female)"]
  10KA_3 = female pin header, 3 pins [form="♀ (female)"]
  R57 = Resistor [tolerance=±5% resistance=5.6k package=THT]
  C43 = Ceramic Capacitor [capacitance=100nF package="100 mil [THT, multilayer]"]
  C44 = Electrolytic Capacitor [capacitance=2.2µF package="100 mil [THT, electrolytic]"]
  10KA_4 = female pin header, 3 pins [form="♀ (female)"]
  J5 = female pin header, 2 pins [form="♀ (female)" part_number="AUDIO OUT"]
  R58 = Resistor [tolerance=±5% resistance=5.6k package=THT]
  C45 = Ceramic Capacitor [capacitance=100nF package="100 mil [THT, multilayer]"]
  10KA2 = female pin header, 3 pins [form="♀ (female)"]
  R59 = Resistor [tolerance=±5% resistance=22k package=THT]
  IC6 = LM324 [package=dil16]
  C46 = Electrolytic Capacitor [capacitance=2.2µF package="100 mil [THT, electrolytic]"]
  R60 = Resistor [tolerance=±5% resistance=10k package=THT]
  R61 = Resistor [tolerance=±5% resistance=100k package=THT]
  C47 = Ceramic Capacitor [capacitance=82pF package="100 mil [THT, multilayer]"]
  R62 = Resistor [tolerance=±5% resistance=100k package=THT]
  C48 = Ceramic Capacitor [capacitance=100nF package="100 mil [THT, multilayer]"]
  10KA_5 = female pin header, 3 pins [form="♀ (female)"]
  C49 = Electrolytic Capacitor [capacitance=2.2µF package="100 mil [THT, electrolytic]"]
  C23 = Electrolytic Capacitor [capacitance=2.2µF package="100 mil [THT, electrolytic]"]
  C50 = Electrolytic Capacitor [capacitance=2.2µF package="100 mil [THT, electrolytic]"]
  R63 = Resistor [tolerance=±5% resistance=100k package=THT]
  C51 = Ceramic Capacitor [capacitance=100nF package="100 mil [THT, multilayer]"]
  C52 = Ceramic Capacitor [capacitance=100nF package="100 mil [THT, multilayer]"]
  R64 = Resistor [tolerance=±5% resistance=100k package=THT]
  R65 = Resistor [tolerance=±5% resistance=100k package=THT]
  R66 = Resistor [tolerance=±5% resistance=100k package=THT]
  R67 = Resistor [tolerance=±5% resistance=100k package=THT]
  C53 = Ceramic Capacitor [capacitance=82pF package="100 mil [THT, multilayer]"]
  C54 = Ceramic Capacitor [capacitance=82pF package="100 mil [THT, multilayer]"]
  SWITCH_FILTER_SHUNT = female pin header, 3 pins [form="♀ (female)"]
  R68 = Resistor [tolerance=±5% resistance=100k package=THT]
  R69 = Resistor [tolerance=±5% resistance=100k package=THT]
  R70 = Resistor [tolerance=±5% resistance=100k package=THT]
  C55 = Ceramic Capacitor [capacitance=100nF package="100 mil [THT, multilayer]"]
  J6 = female pin header, 2 pins [form="♀ (female)" part_number="AUX IN"]
  R71 = Resistor [tolerance=±5% resistance=100k package=THT]
  ANALOG_INS = female pin header, 9 pins [form="♀ (female)"]
  AUDIO_DIFF_IN = female pin header, 3 pins [form="♀ (female)"]
  POWER_OUT = female pin header, 4 pins [form="♀ (female)"]
  J7 = female pin header, 2 pins [form="♀ (female)" part_number="AUDIO OUT"]
  R72 = Resistor [tolerance=±5% resistance=220 package=THT]
  R73 = Resistor [tolerance=±5% resistance=10k package=THT]
  R74 = Resistor [tolerance=±5% resistance=220 package=THT]
  EXPRESSION_PEDAL_INPUT = female pin header, 3 pins [form="♀ (female)"]
  R75 = Resistor [tolerance=±5% resistance=220 package=THT]
  SUSTAIN_PEDAL_INPUT = female pin header, 2 pins [form="♀ (female)"]
  R76 = Resistor [tolerance=±5% resistance=10k package=THT]
  Q21 = NPN-Transistor [part_number=BC548 package="TO92 [THT]"]
  R77 = Resistor [tolerance=±5% resistance=10k package=THT]
  SYNC_IN = female pin header, 2 pins [form="♀ (female)"]
  R78 = Resistor [tolerance=±5% resistance=100k package=THT]
  Q22 = NPN-Transistor [part_number=BC548 package="TO92 [THT]"]
  R79 = Resistor [tolerance=±5% resistance=10k package=THT]
  R80 = Resistor [tolerance=±5% resistance=1k package=THT]
  SYNC_OUT = female pin header, 2 pins [form="♀ (female)"]
  R81 = Resistor [tolerance=±5% resistance=1M package=THT]
  OLED = female pin header, 7 pins [form="♀ (female)"]
  ARDUINO_SPI = female pin header, 3 pins [form="♀ (female)"]
  SDCARD = female pin header, 6 pins [form="♀ (female)"]
  R82 = Resistor [tolerance=±5% resistance=1k package=THT]
  R83 = Resistor [tolerance=±5% resistance=1k package=THT]

nets:
  N1: Componente1.A8, ANALOG_INS.pin4
  N2: Componente1.A9, ANALOG_INS.pin3
  N3: Componente1.A10, ANALOG_INS.pin2
  N4: Componente1.A11, ANALOG_INS.pin1
  AUDIO_OUT_1: Componente1.DAC0, C51.1
  AUDIO_OUT_2: Componente1.DAC1, C52.1
  AUDIO_IN_1: Componente1.A0, AUDIO_DIFF_IN.pin3
  AUDIO_IN_2: Componente1.A1, AUDIO_DIFF_IN.pin1
  PEDAL_EXP: Componente1.A2, R74.Pin_0
  N5: Componente1.A3, ANALOG_INS.pin9
  N6: Componente1.A4, ANALOG_INS.pin8
  N7: Componente1.A5, ANALOG_INS.pin7
  N8: Componente1.A6, ANALOG_INS.pin6
  N9: Componente1.A7, ANALOG_INS.pin5
  TX_MIDI: Componente1.D16/TX2, R35.Pin_0
  RX_MIDI: Componente1.D17/RX2, U2.Pin_5, R31.Pin_0
  I2C_SDA: Componente1.D20/SDA3, IC4.pin5
  I2C_SCL: Componente1.D21/SCL3, IC4.pin6
  3.3V: Componente1.IOREF, R31.Pin_1, IC4.pin8, POWER_OUT.pin4, R73.Pin_1, R75.Pin_1, R76.Pin_1, OLED.pin2
  N10: Componente1.MASTER-RESET, C35.+
  5V: Componente1.5V, Q7.C, Q8.C, Q9.C, Q10.C, R32.Pin_1, R34.Pin_0, Q18.C, Q20.C, POWER_OUT.pin3, R80.Pin_1, SDCARD.pin2
  GND: Componente1.GND, Q1.source, Q2.source, Q3.source, Q4.source, C1.0, C2.0, C3.0, C4.0, C7.0, C8.1, C9.1, C10.1, C13.0, C14.0, C15.0, C16.0, IC1.GND, C19.0, C20.-, C21.0, C22.-, J2.pin2, U2.Pin_4, R23.Pin_1, R25.Pin_1, Q15.E, Q16.E, R37.Pin_0, C28.-, IC4.pin1, IC4.pin2, IC4.pin3, IC4.pin4, IC4.pin7, Q17.source, C29.0, Q19.source, C30.0, C31.1, C32.1, C33.0, C34.0, ENCODER_A.pin2, C35.-, ENCODER_B.pin2, ENCODER_C.pin2, ENCODER_D.pin2, IC5.GND, 10KA_2.pin1, 10KA_3.pin1, C43.0, 10KA_4.pin1, J5.pin2, C45.0, 10KA2.pin1, IC6.GND, 10KA_5.pin1, R63.Pin_0, J6.pin1, AUDIO_DIFF_IN.pin2, POWER_OUT.pin1, J7.pin1, EXPRESSION_PEDAL_INPUT.pin3, SUSTAIN_PEDAL_INPUT.pin2, Q21.E, SYNC_IN.pin2, R78.Pin_1, Q22.E, SYNC_OUT.pin2, R81.Pin_0, OLED.pin1, SDCARD.pin1, R83.Pin_0
  9V: Componente1.VIN, IC1.OUT, C19.1, C20.+, R20.Pin_0, R36.Pin_0, IC5.V+, 10KA_2.pin3, IC6.V+, POWER_OUT.pin2
  VCA_5: Componente1.D10_PWM/SS0, R43.Pin_0
  VCA_4: Componente1.D11_PWM, R42.Pin_0
  ADSR_FILTER: Componente1.D12_PWM, R57.Pin_0
  LFO_OUT: Componente1.D13_PWM, R58.Pin_0
  VCA_3: Componente1.D2_PWM, R8.Pin_0
  VCA_2: Componente1.D3_PWM, R7.Pin_0
  VCA_1: Componente1.D4_PWM/SS1, R6.Pin_0
  VCA_0: Componente1.D5_PWM, R5.Pin_0
  VOICE_4: Componente1.D6_PWM, Q17.gate
  VOICE_5: Componente1.D7_PWM, Q19.gate
  ENCODER_A_1: Componente1.D33, ENCODER_A.pin1
  VOICE_0: Componente1.D34, Q1.gate
  ENCODER_A_2: Componente1.D35, ENCODER_A.pin3
  VOICE_1: Componente1.D36, Q2.gate
  ENCODER_B_1: Componente1.D37, ENCODER_B.pin1
  VOICE_2: Componente1.D38, Q3.gate
  ENCODER_B_2: Componente1.D39, ENCODER_B.pin3
  VOICE_3: Componente1.D40, Q4.gate
  ENCODER_C_1: Componente1.D41, ENCODER_C.pin1
  ENCODER_C_2: Componente1.D43, ENCODER_C.pin3
  ENCODER_D_1: Componente1.D45, ENCODER_D.pin1
  PEDAL_SUS: Componente1.D46, R72.Pin_0
  ENCODER_D_2: Componente1.D47, ENCODER_D.pin3
  SYNC_IN: Componente1.D48, R76.Pin_0, Q21.C
  LCD_RES: Componente1.D49, LCD_CONN.pin1, OLED.pin5
  SYNC_OUT: Componente1.D50, R79.Pin_0
  LCD_DC: Componente1.D51, LCD_CONN.pin3, OLED.pin6
  LCD_CS: Componente1.D53, LCD_CONN.pin2, OLED.pin7
  N11: Q1.drain, R1.Pin_0, R16.Pin_0
  N12: Q2.drain, R2.Pin_0, R15.Pin_0
  N13: Q3.drain, R3.Pin_0, R14.Pin_0
  N14: Q4.drain, R4.Pin_0, R13.Pin_0
  N15: R1.Pin_1, C1.1, Q7.E
  N16: R2.Pin_1, C2.1, Q8.E
  N17: R3.Pin_1, C3.1, Q9.E
  N18: R4.Pin_1, C4.1, Q10.E
  N19: R5.Pin_1, Q7.B, C7.1
  N20: R6.Pin_1, Q8.B, C8.0
  N21: R7.Pin_1, Q9.B, C9.0
  N22: R8.Pin_1, Q10.B, C10.0
  N23: R13.Pin_1, C16.1, C38.1
  N24: R14.Pin_1, C15.1, C39.1
  N25: R15.Pin_1, C14.1, C40.1
  N26: R16.Pin_1, C13.1, C41.1
  N27: IC1.IN, C21.1
  N28: C22.+, J2.pin1
  N29: U2.Pin_1, D6.C, R19.Pin_0
  N30: U2.Pin_2, J3.pin2, D6.A
  N31: J3.pin1, R19.Pin_1
  N32: Q13.E, Q14.E, R23.Pin_0
  N33: Q13.B, R26.Pin_1, R29.Pin_1, R30.Pin_1, R59.Pin_1
  N34: Q13.C, D10.C, R22.Pin_1
  4.5V/POS_1/POS_5: Q14.B, R26.Pin_0, R27.Pin_1, R36.Pin_1, R37.Pin_1, C28.+, IC5.IN1+, R56.Pin_0, IC6.IN1+, R67.Pin_0, C54.0
  N35: Q14.C, D7.A, R21.Pin_1
  N36: D7.C, D8.A, C24.1
  N37: D8.C, D9.A, C25.1, C27.0
  N38: D9.C, D10.A, C26.1
  N39: R20.Pin_1, R21.Pin_0, R22.Pin_0
  N40: C24.0, C26.0, R24.Pin_0
  N41: C25.0, R25.Pin_0, C23.-
  FILTER_OUT/OUT_3: R24.Pin_1, IC5.OUT3, 10KA.pin1, C46.+
  POS_3: C27.1, R27.Pin_0, IC5.IN3+
  N42: R29.Pin_0, 10KA_2.pin2
  N43: R30.Pin_0, 10KA_3.pin2
  N44: Q15.B, R35.Pin_1
  N45: Q15.C, Q16.B, R32.Pin_0
  N46: Q16.C, R33.Pin_0
  N47: R33.Pin_1, J4.pin2
  N48: R34.Pin_1, J4.pin1
  N49: Q17.drain, R40.Pin_0, R44.Pin_0
  N50: Q18.E, R40.Pin_1, C29.1
  N51: Q18.B, R42.Pin_1, C31.0
  N52: Q19.drain, R41.Pin_0, R45.Pin_0
  N53: R41.Pin_1, Q20.E, C30.1
  N54: Q20.B, R43.Pin_1, C32.0
  N55: R44.Pin_1, C33.1, C37.1
  N56: R45.Pin_1, C34.1, C36.1
  OUT_1: IC5.OUT1, R52.Pin_1, C42.0, R53.Pin_0
  NEG_1: IC5.IN1-, R46.Pin_1, R47.Pin_1, R48.Pin_1, R49.Pin_1, R50.Pin_1, R51.Pin_1, R52.Pin_0, C42.1, R62.Pin_1
  POS_2: IC5.IN2+, R57.Pin_1, C43.1
  NEG_2/OUT_2: IC5.IN2-, IC5.OUT2, 10KA_3.pin3
  NEG_3: IC5.IN3-, R55.Pin_0, R56.Pin_1
  POS_4: IC5.IN4+, R58.Pin_1, C45.1, IC6.IN4+
  NEG_4/OUT_4: IC5.IN4-, IC5.OUT4, 10KA2.pin3
  N57: C36.0, R46.Pin_0
  N58: C37.0, R47.Pin_0
  N59: C38.0, R48.Pin_0
  N60: C39.0, R49.Pin_0
  N61: R50.Pin_0, C40.0
  N62: C41.0, R51.Pin_0
  VCO_OUT: R53.Pin_1, C23.+
  N63: R55.Pin_1, 10KA.pin2, 10KA.pin3
  N64: C44.-, J5.pin1, R63.Pin_1
  OUT_7: C44.+, IC6.OUT3, R70.Pin_1
  N65: 10KA_4.pin2, C55.1
  N66: 10KA_4.pin3, C50.-
  N67: 10KA2.pin2, R59.Pin_0
  OUT_5: IC6.OUT1, R61.Pin_1, C47.0, C50.+, J7.pin2
  NEG_5: IC6.IN1-, R60.Pin_1, R61.Pin_0, C47.1, R68.Pin_1, R71.Pin_1
  POS_6: IC6.IN2+, R65.Pin_1, R67.Pin_1, C54.1
  NEG_6: IC6.IN2-, R64.Pin_1, R66.Pin_0, C53.1
  OUT_6: IC6.OUT2, C49.+, R66.Pin_1, C53.0
  NEG_7: IC6.IN3-, R69.Pin_1, R70.Pin_0
  POS_7: IC6.IN3+
  NEG_8: IC6.IN4-
  OUT_8: IC6.OUT4
  N68: C46.-, R60.Pin_0
  N69: R62.Pin_0, SWITCH_FILTER_SHUNT.pin3
  N70: C48.0, 10KA_5.pin2
  N71: C48.1, SWITCH_FILTER_SHUNT.pin2
  N72: 10KA_5.pin3, C49.-
  N73: C51.0, R64.Pin_0
  N74: C52.0, R65.Pin_0
  N75: SWITCH_FILTER_SHUNT.pin1, R68.Pin_0
  N76: R69.Pin_0, C55.0
  N77: J6.pin2, R71.Pin_0
  N78: R72.Pin_1, R73.Pin_0, SUSTAIN_PEDAL_INPUT.pin1
  N79: R74.Pin_1, EXPRESSION_PEDAL_INPUT.pin2, R81.Pin_1
  N80: EXPRESSION_PEDAL_INPUT.pin1, R75.Pin_0
  N81: Q21.B, R77.Pin_0, R78.Pin_0
  N82: R77.Pin_1, SYNC_IN.pin1
  N83: Q22.B, R79.Pin_1
  N84: Q22.C, R80.Pin_0, SYNC_OUT.pin1
  CLK: OLED.pin3, ARDUINO_SPI.pin2, SDCARD.pin5
  MOSI: OLED.pin4, ARDUINO_SPI.pin1, SDCARD.pin4
  MISO: ARDUINO_SPI.pin3, R82.Pin_0, R83.Pin_1
  N85: SDCARD.pin3, R82.Pin_1
  SD_CS: SDCARD.pin6

notes:
  MIDI IN
  CUTOFF
  MIDI OUT
  LM324_1
  RESONANCE
  ADSR DEEP
  MASTER VOL
  LFO DEEP
  SAMPLES/FX VOLUME

custom parts:
  2N7000 FET N-Channel: A 2N7000 MOSFET N-Channel Transistor
  LM324: LM324 Quad OpAmp
